# Fritzing sketch uhppoted-wiegand-pico (saved by Fritzing 0.9.10b)
breadboards: 2

parts:
  Mod1 = Raspberry Pi Pico  # not connected
  M1 = RioRand LM2596
  J1 = female pin header, 2 pins [form="♀ (female)"]
  Part1 = Adafruit 4-channel I2C-safe Bi-directional Logic Level Converter [part_number="Adafruit #757"]
  J2 = female pin header, 2 pins [form="♀ (female)"]

nets:
  N1: M1.Pin_1, J1.pin2
  N2: M1.Pin_2, M1.Pin_4, J1.pin1, Part1.GND, J2.pin1
  N3: M1.Pin_3, Part1.HV, J2.pin2

custom parts:
  Raspberry Pi Pico: Raspberry Pi Pico. Based around the RP2040 microcontroller the Pico is a low cost microcontroller device bringing Raspberry Pi quality, cost, and easy of use to the microcontroller space. Jan 2021, Split part in to two versions: tht (this one) and SMD. This one will drill holes for a .1 in header in pcb to allow plugging in the module as well as providing pads to solder the module to the top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
  Adafruit 4-channel I2C-safe Bi-directional Logic Level Converter: Because the Arduino (and Basic Stamp) are 5V devices, and most modern sensors, displays, flash cards and modes are 3.3V-only, many makers find that they need to perform level shifting/conversion to protect the 3.3V device from 5V. We do have some other handy level shifters in the shop, from the DIP 74LVC245 to the fancy bi-directional TXB0108. However, neither of these are happy to work with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
